# Fritzing sketch Raspberry Pi Pico - Circuit Connection Diagram (saved by Fritzing 1.0.6)
perfboards: 1

parts:
  A1 = Raspberry Pi Pico2

nets:
  N1: A1.pin_3, A1.pin_8, A1.pin_13, A1.pin_18, A1.pin_23, A1.pin_28, A1.pin_33, A1.pin_38

notes:
  Raspberry Pi Pico - Circuit Connection Diagram
  5V - vcc for Ultrasonic sensor
  GND - gnd for Ultrasonic sensor
  Servo motor
  Signal Pin : GP26 | brown,
  Ultrasonic trigger and echo pins :
  Right Trig - GP18 | yellow
  Right Echo - GP19 | green
  Left Trig - GP20 | yellow
  Left Echo - GP21 | green
  Emergency Button Pin - GP16 |Red
  Limit switch Pins : Orange
  Switch 1 : GP03
  Switch 2 : GP02
  Switch 3 : GP04
  5x GND pins
  Stepper motor pins
  DIR : blue | PUL :white
  motor 1 | Base motor
  DIR : GP09 | PUL : GP11
  motor 2 | Shoulder motor
  DIR : GP07 | PUL : GP13
  motor 3 | Elbow motor
  DIR : GP14 | PUL : GP15

custom parts:
  Raspberry Pi Pico2: Raspberry Pi Pico 2W is our new $7 microcontroller board, built on RP2350: our new high-performance, secure microcontroller with on board WiFi.
